// Logisim project plans.circ as structural Verilog
module main (
);

  wire [7:0] AX_q, BX_q, EIP_q, IP_q, multiplexer_1_out, multiplexer_2_out, ram_unit_1_p2, ram_unit_1_p4;
  wire [23:0] IR_q, multiplexer_3_out, ram_unit_1_p3, rom_1_data;

  Register IP (.Q(IP_q));  // open: D, en, clk, clr
  Register EIP (.Q(EIP_q));  // open: D, en, clk, clr
  ROM #(.dataWidth(24)) rom_1 (.addr(EIP_q), .data(rom_1_data));
  Register AX (.D(ram_unit_1_p2), .Q(AX_q));  // open: en, clk, clr
  Register BX (.D(ram_unit_1_p2), .Q(BX_q));  // open: en, clk, clr
  // RAM_unit ram_unit_1: pin names not known; wires that end beside it: IP_q, ram_unit_1_p2, ram_unit_1_p3, ram_unit_1_p4
  Multiplexer #(.select(2), .width(8)) multiplexer_1 (
    .in0(AX_q), .in1(BX_q), .in2(ram_unit_1_p4), .out(multiplexer_1_out));  // open: in3, sel
  Multiplexer #(.select(2), .width(8)) multiplexer_2 (
    .in0(AX_q), .in1(BX_q), .in2(ram_unit_1_p4), .out(multiplexer_2_out));  // open: in3, sel
  Register #(.width(24)) IR (.D(multiplexer_3_out), .Q(IR_q));  // open: en, clk, clr
  Multiplexer #(.width(24)) multiplexer_3 (
    .in0(ram_unit_1_p3), .in1(rom_1_data), .out(multiplexer_3_out));  // open: sel
  instruction_decoder instruction_decoder_1 (.instruction(IR_q));
  exception_handler exception_handler_1 ();
  main_controller main_controller_1 ();
  ALU alu_1 (.A(multiplexer_1_out), .B(multiplexer_2_out), .result(ram_unit_1_p2));
endmodule

module ALU (
  input  [7:0] A,
  input  [7:0] B,
  output [7:0] result
);
endmodule

module instruction_decoder (
  input  [23:0] instruction
);
endmodule

module RAM_unit (
  input  [7:0] instruction_address_tri_word,
  input  instuction_request,
  input  [7:0] operation_address_one_word,
  input  [7:0] operation_data,
  input  operation_R_or_w,
  input  operation_request,
  output instruction_ready,
  output [23:0] instruction_out,
  output operation_ready,
  output [7:0] operation_out
);
endmodule
